// Logisim project ALU_Andres_y_Daniel.circ as structural Verilog: 16 circuits, main circuit ALU_32
module ALU_32_bit (
  input  [31:0] A,
  input  [31:0] B,
  input  [4:0] op,
  output negative,
  output overflow,
  output [31:0] out1
);

  wire add_overflow, addi_overflow;
  wire [31:0] add_result, addi_result, and1_result, beq1_out_3, bgt1_gto, blt1_lto, bne1_out_3, div_o, j_o,
       jal_o, jr_o, la_o, li_o, lw_result, mfhi_o, mflo_o, move_o, mult_o, or1_result, sll1_o, srl1_o,
       sub_result, sw_result;

  L_32_bit_Adder add (.A(A), .B(B), .overflow(add_overflow), .Result(add_result));
  L_32_bit_Subtractor sub (.A(A), .B(B), .negative(negative), .Result(sub_result));
  L_32_bit_Adder addi (.A(A), .B(B), .overflow(addi_overflow), .Result(addi_result));
  L_32_Pass mult (.a(A), .b(B), .o(mult_o));
  L_32_Pass div (.a(A), .b(B), .o(div_o));
  L_32_Pass mfhi (.a(A), .b(B), .o(mfhi_o));
  L_32_Pass mflo (.a(A), .b(B), .o(mflo_o));
  L_32_bit_AND and1 (.A(A), .B(B), .Result(and1_result));
  L_32_bit_OR or1 (.A(A), .B(B), .Result(or1_result));
  L_32_Pass sll1 (.a(A), .b(B), .o(sll1_o));
  L_32_Pass srl1 (.a(A), .b(B), .o(srl1_o));
  L_32_Pass j (.a(A), .b(B), .o(j_o));
  L_32_Pass jal (.a(A), .b(B), .o(jal_o));
  L_32_Pass jr (.a(A), .b(B), .o(jr_o));
  beq beq1 (.a(A), .b(B), .out_3(beq1_out_3));
  bne bne1 (.in_1(A), .in_2(B), .out_3(bne1_out_3));
  bgt bgt1 (.a(A), .b(B), .gto(bgt1_gto));
  blt blt1 (.a(A), .b(B), .lto(blt1_lto));
  L_32_Pass move (.a(A), .b(B), .o(move_o));
  L_32_Pass li (.a(A), .b(B), .o(li_o));
  L_32_Pass la (.a(A), .b(B), .o(la_o));
  L_32_bit_Adder lw (.A(A), .B(B), .Result(lw_result));  // open: overflow
  L_32_bit_Adder sw (.A(A), .B(B), .Result(sw_result));  // open: overflow
  or or_1 (overflow, add_overflow, addi_overflow);
  Multiplexer #(.enable("false"), .select(5), .width(32)) multiplexer_1 (
    .in0(add_result), .in1(sub_result), .in2(addi_result), .in3(mult_o), .in4(div_o), .in5(mfhi_o),
    .in6(mflo_o), .in7(and1_result), .in8(or1_result), .in9(sll1_o), .in10(srl1_o), .in11(j_o), .in12(jal_o),
    .in13(jr_o), .in14(beq1_out_3), .in15(bne1_out_3), .in16(bgt1_gto), .in17(blt1_lto), .in18(move_o),
    .in19(li_o), .in20(la_o), .in21(lw_result), .in22(sw_result), .out(out1), .sel(op));  // open: in23, in24, in25, in26, in27, in28, in29, in30, in31
endmodule

// +
module L_1_bit_Adder (
  input  A,
  input  B,
  input  Carry_In,
  output Carry_Out,
  output Result
);

  wire and_1_out, and_2_out, xor_1_out;

  and and_1 (and_1_out, A, B);
  xor xor_1 (xor_1_out, A, B);
  or or_1 (Carry_Out, and_1_out, and_2_out);
  and and_2 (and_2_out, Carry_In, xor_1_out);
  xor xor_2 (Result, Carry_In, xor_1_out);

  // Notes on the sheet:
  //   Full Adder
endmodule

module L_4_bit_Adder (
  input  [3:0] A,
  input  [3:0] B,
  input  Carry_In,
  output Carry_Out,
  output [3:0] Result
);

  wire l_1_bit_adder_1_carry_out, l_1_bit_adder_2_carry_out, l_1_bit_adder_3_carry_out;

  L_1_bit_Adder l_1_bit_adder_1 (
    .A(A[0]), .B(B[0]), .Carry_Out(l_1_bit_adder_1_carry_out), .Carry_In(Carry_In), .Result(Result[0]));
  L_1_bit_Adder l_1_bit_adder_2 (
    .A(A[1]), .B(B[1]), .Carry_Out(l_1_bit_adder_2_carry_out), .Carry_In(l_1_bit_adder_1_carry_out),
    .Result(Result[1]));
  L_1_bit_Adder l_1_bit_adder_3 (
    .A(A[2]), .B(B[2]), .Carry_Out(l_1_bit_adder_3_carry_out), .Carry_In(l_1_bit_adder_2_carry_out),
    .Result(Result[2]));
  L_1_bit_Adder l_1_bit_adder_4 (
    .A(A[3]), .B(B[3]), .Carry_Out(Carry_Out), .Carry_In(l_1_bit_adder_3_carry_out), .Result(Result[3]));
endmodule

module L_16_bit_Adder (
  input  [15:0] A,
  input  [15:0] B,
  input  Carry_In,
  output Carry_Out,
  output [15:0] Result
);

  wire l_4_bit_adder_1_carry_out, l_4_bit_adder_2_carry_out, l_4_bit_adder_3_carry_out;

  L_4_bit_Adder l_4_bit_adder_1 (
    .Carry_In(Carry_In), .A(A[3:0]), .B(B[3:0]), .Result(Result[3:0]), .Carry_Out(l_4_bit_adder_1_carry_out));
  L_4_bit_Adder l_4_bit_adder_2 (
    .Carry_In(l_4_bit_adder_1_carry_out), .A(A[7:4]), .B(B[7:4]), .Result(Result[7:4]),
    .Carry_Out(l_4_bit_adder_2_carry_out));
  L_4_bit_Adder l_4_bit_adder_3 (
    .Carry_In(l_4_bit_adder_2_carry_out), .A(A[11:8]), .B(B[11:8]), .Result(Result[11:8]),
    .Carry_Out(l_4_bit_adder_3_carry_out));
  L_4_bit_Adder l_4_bit_adder_4 (
    .Carry_In(l_4_bit_adder_3_carry_out), .A(A[15:12]), .B(B[15:12]), .Result(Result[15:12]),
    .Carry_Out(Carry_Out));
endmodule

module L_32_bit_AND (
  input  [31:0] A,
  input  [31:0] B,
  output [31:0] Result
);

  assign Result = A & B;  // AND_Gate and_1, 32 bits wide

  // Notes on the sheet:
  //   32-bit AND
endmodule

module L_32_bit_OR (
  input  [31:0] A,
  input  [31:0] B,
  output [31:0] Result
);

  assign Result = A | B;  // OR_Gate or_1, 32 bits wide

  // Notes on the sheet:
  //   32-bit OR
endmodule

module L_32_bit_Adder_Subtracter (
  input  [31:0] A,
  input  [31:0] B,
  input  Carry_In,
  output Carry_Out,
  output [31:0] Result
);

  wire l_16_bit_adder_1_carry_out;
  wire [15:0] bit_extender_1_out, xor_1_out, xor_2_out;

  assign bit_extender_1_out = {{15{Carry_In}}, Carry_In};  // Bit_Extender bit_extender_1
  assign xor_1_out = bit_extender_1_out ^ B[15:0];  // XOR_Gate xor_1, 16 bits wide
  L_16_bit_Adder l_16_bit_adder_1 (
    .Carry_In(Carry_In), .A(A[15:0]), .B(xor_1_out), .Result(Result[15:0]),
    .Carry_Out(l_16_bit_adder_1_carry_out));
  assign xor_2_out = bit_extender_1_out ^ B[31:16];  // XOR_Gate xor_2, 16 bits wide
  L_16_bit_Adder l_16_bit_adder_2 (
    .Carry_In(l_16_bit_adder_1_carry_out), .A(A[31:16]), .B(xor_2_out), .Result(Result[31:16]),
    .Carry_Out(Carry_Out));

  // Notes on the sheet:
  //   32 bit Adder/Subtracter
endmodule

module L_32_bit_Subtractor (
  input  [31:0] A,
  input  [31:0] B,
  output negative,
  output [31:0] Result
);

  wire l_32_bit_adder_subtracter_1_carry_out;

  not not_1 (negative, l_32_bit_adder_subtracter_1_carry_out);
  L_32_bit_Adder_Subtracter l_32_bit_adder_subtracter_1 (
    .A(A), .B(B), .Carry_Out(l_32_bit_adder_subtracter_1_carry_out), .Carry_In(1'b1), .Result(Result));
endmodule

module L_32_bit_Adder (
  input  [31:0] A,
  input  [31:0] B,
  output overflow,
  output [31:0] Result
);

  L_32_bit_Adder_Subtracter l_32_bit_adder_subtracter_1 (
    .A(A), .B(B), .Carry_Out(overflow), .Result(Result));  // open: Carry_In
endmodule

module L_32_Pass (
  input  [31:0] a,
  input  [31:0] b,
  output [31:0] o
);


  assign o = b;
endmodule

module ALU_32 (
  input  [31:0] in_1,
  input  [31:0] in_2,
  input  [4:0] in_3,
  output out_4,
  output out_5,
  output [31:0] out_6
);

  ALU_32_bit alu_32_bit_1 (.A(in_1), .B(in_2), .op(in_3), .negative(out_4), .overflow(out_5), .out1(out_6));
endmodule

module beq (
  input  [31:0] a,
  input  [31:0] b,
  output [31:0] out_3
);

  wire and_1_out;
  wire [31:0] xnor_1_out;

  assign xnor_1_out = ~(a ^ b);  // XNOR_Gate xnor_1, 32 bits wide
  and and_1 (and_1_out, xnor_1_out[0], xnor_1_out[1], xnor_1_out[2], xnor_1_out[3], xnor_1_out[4], xnor_1_out[5], xnor_1_out[6], xnor_1_out[7], xnor_1_out[8], xnor_1_out[9], xnor_1_out[10], xnor_1_out[11], xnor_1_out[12], xnor_1_out[13], xnor_1_out[14], xnor_1_out[15], xnor_1_out[17], xnor_1_out[18], xnor_1_out[19], xnor_1_out[20], xnor_1_out[21], xnor_1_out[22], xnor_1_out[23], xnor_1_out[24], xnor_1_out[25], xnor_1_out[26], xnor_1_out[27], xnor_1_out[28], xnor_1_out[29], xnor_1_out[30], xnor_1_out[31], xnor_1_out[16]);
  assign out_3 = {{31{and_1_out}}, and_1_out};  // Bit_Extender bit_extender_1
endmodule

module bne (
  input  [31:0] in_1,
  input  [31:0] in_2,
  output [31:0] out_3
);

  wire [31:0] beq_1_out_3;

  beq beq_1 (.a(in_1), .b(in_2), .out_3(beq_1_out_3));
  assign out_3 = ~beq_1_out_3;  // NOT_Gate not_1, 32 bits wide
endmodule

module comp4 (
  input  [3:0] a,
  input  [3:0] b,
  input  gti,
  input  eqi,
  input  lti,
  output gto,
  output eqo,
  output lto
);

  wire and_3_out, and_4_out, and_5_out, and_6_out, and_7_out, nand_1_out, or_1_out, or_2_out;
  wire [3:0] and_1_out, and_2_out, not_1_out, not_2_out, xnor_1_out;

  assign not_1_out = ~a;  // NOT_Gate not_1, 4 bits wide
  assign and_1_out = a & not_2_out;  // AND_Gate and_1, 4 bits wide
  assign not_2_out = ~b;  // NOT_Gate not_2, 4 bits wide
  assign xnor_1_out = ~(b ^ a);  // XNOR_Gate xnor_1, 4 bits wide
  assign and_2_out = not_1_out & b;  // AND_Gate and_2, 4 bits wide
  or or_1 (or_1_out, and_1_out[0], and_1_out[1], and_1_out[3], and_1_out[2]);
  and and_3 (and_3_out, xnor_1_out[0], xnor_1_out[1], xnor_1_out[3], xnor_1_out[2]);
  or or_2 (or_2_out, and_2_out[0], and_2_out[1], and_2_out[3], and_2_out[2]);
  and and_4 (and_4_out, gti, and_3_out);
  and and_5 (and_5_out, and_3_out, eqi);
  and and_6 (and_6_out, and_3_out, lti);
  or or_3 (gto, or_1_out, and_4_out);
  or or_4 (lto, and_6_out, or_2_out);
  nand nand_1 (nand_1_out, gti, eqi, lti);
  and and_7 (and_7_out, nand_1_out, and_3_out);
  or or_5 (eqo, and_5_out, and_7_out);
endmodule

module bgt (
  input  [31:0] a,
  input  [31:0] b,
  output [31:0] gto
);

  wire comp4_1_eqo, comp4_1_gto, comp4_1_lto, comp4_2_eqo, comp4_2_gto, comp4_2_lto, comp4_3_eqo,
       comp4_3_gto, comp4_3_lto, comp4_4_eqo, comp4_4_gto, comp4_4_lto, comp4_5_eqo, comp4_5_gto,
       comp4_5_lto, comp4_6_eqo, comp4_6_gto, comp4_6_lto, comp4_7_eqo, comp4_7_gto, comp4_7_lto,
       comp4_8_eqo, comp4_8_gto, comp4_8_lto;

  comp4 comp4_1 (
    .a(a[3:0]), .b(b[3:0]), .gto(comp4_1_gto), .eqo(comp4_1_eqo), .lto(comp4_1_lto));  // open: gti, eqi, lti
  comp4 comp4_2 (
    .a(a[7:4]), .b(b[7:4]), .gti(comp4_1_gto), .eqi(comp4_1_eqo), .lti(comp4_1_lto), .gto(comp4_2_gto),
    .eqo(comp4_2_eqo), .lto(comp4_2_lto));
  comp4 comp4_3 (
    .a(a[11:8]), .b(b[11:8]), .gti(comp4_2_gto), .eqi(comp4_2_eqo), .lti(comp4_2_lto), .gto(comp4_3_gto),
    .eqo(comp4_3_eqo), .lto(comp4_3_lto));
  comp4 comp4_4 (
    .a(a[15:12]), .b(b[15:12]), .gti(comp4_3_gto), .eqi(comp4_3_eqo), .lti(comp4_3_lto), .gto(comp4_4_gto),
    .eqo(comp4_4_eqo), .lto(comp4_4_lto));
  comp4 comp4_5 (
    .a(a[19:16]), .b(b[19:16]), .gti(comp4_4_gto), .eqi(comp4_4_eqo), .lti(comp4_4_lto), .gto(comp4_5_gto),
    .eqo(comp4_5_eqo), .lto(comp4_5_lto));
  comp4 comp4_6 (
    .a(a[23:20]), .b(b[23:20]), .gti(comp4_5_gto), .eqi(comp4_5_eqo), .lti(comp4_5_lto), .gto(comp4_6_gto),
    .eqo(comp4_6_eqo), .lto(comp4_6_lto));
  comp4 comp4_7 (
    .a(a[27:24]), .b(b[27:24]), .gti(comp4_6_gto), .eqi(comp4_6_eqo), .lti(comp4_6_lto), .gto(comp4_7_gto),
    .eqo(comp4_7_eqo), .lto(comp4_7_lto));
  comp4 comp4_8 (
    .a(a[31:28]), .b(b[31:28]), .gti(comp4_7_gto), .eqi(comp4_7_eqo), .lti(comp4_7_lto), .gto(comp4_8_gto),
    .eqo(comp4_8_eqo), .lto(comp4_8_lto));
  assign gto = {{31{comp4_8_gto}}, comp4_8_gto};  // Bit_Extender bit_extender_1
endmodule

module blt (
  input  [31:0] a,
  input  [31:0] b,
  output [31:0] lto
);

  wire comp4_1_eqo, comp4_1_gto, comp4_1_lto, comp4_2_eqo, comp4_2_gto, comp4_2_lto, comp4_3_eqo,
       comp4_3_gto, comp4_3_lto, comp4_4_eqo, comp4_4_gto, comp4_4_lto, comp4_5_eqo, comp4_5_gto,
       comp4_5_lto, comp4_6_eqo, comp4_6_gto, comp4_6_lto, comp4_7_eqo, comp4_7_gto, comp4_7_lto,
       comp4_8_eqo, comp4_8_gto, comp4_8_lto;

  comp4 comp4_1 (
    .a(a[3:0]), .b(b[3:0]), .gto(comp4_1_gto), .eqo(comp4_1_eqo), .lto(comp4_1_lto));  // open: gti, eqi, lti
  comp4 comp4_2 (
    .a(a[7:4]), .b(b[7:4]), .gti(comp4_1_gto), .eqi(comp4_1_eqo), .lti(comp4_1_lto), .gto(comp4_2_gto),
    .eqo(comp4_2_eqo), .lto(comp4_2_lto));
  comp4 comp4_3 (
    .a(a[11:8]), .b(b[11:8]), .gti(comp4_2_gto), .eqi(comp4_2_eqo), .lti(comp4_2_lto), .gto(comp4_3_gto),
    .eqo(comp4_3_eqo), .lto(comp4_3_lto));
  comp4 comp4_4 (
    .a(a[15:12]), .b(b[15:12]), .gti(comp4_3_gto), .eqi(comp4_3_eqo), .lti(comp4_3_lto), .gto(comp4_4_gto),
    .eqo(comp4_4_eqo), .lto(comp4_4_lto));
  comp4 comp4_5 (
    .a(a[19:16]), .b(b[19:16]), .gti(comp4_4_gto), .eqi(comp4_4_eqo), .lti(comp4_4_lto), .gto(comp4_5_gto),
    .eqo(comp4_5_eqo), .lto(comp4_5_lto));
  comp4 comp4_6 (
    .a(a[23:20]), .b(b[23:20]), .gti(comp4_5_gto), .eqi(comp4_5_eqo), .lti(comp4_5_lto), .gto(comp4_6_gto),
    .eqo(comp4_6_eqo), .lto(comp4_6_lto));
  comp4 comp4_7 (
    .a(a[27:24]), .b(b[27:24]), .gti(comp4_6_gto), .eqi(comp4_6_eqo), .lti(comp4_6_lto), .gto(comp4_7_gto),
    .eqo(comp4_7_eqo), .lto(comp4_7_lto));
  comp4 comp4_8 (
    .a(a[31:28]), .b(b[31:28]), .gti(comp4_7_gto), .eqi(comp4_7_eqo), .lti(comp4_7_lto), .gto(comp4_8_gto),
    .eqo(comp4_8_eqo), .lto(comp4_8_lto));
  assign lto = {{31{comp4_8_lto}}, comp4_8_lto};  // Bit_Extender bit_extender_1
endmodule
